# Fritzing sketch Small_colbs (saved by Fritzing 0.9.3b)

parts:
  Часть2 = Arduino Prototyping Shield
  Q1 = NPN-Transistor [package="TO92 [THT]"]
  Q2 = NPN-Transistor [package="TO92 [THT]"]
  Q3 = NPN-Transistor [package="TO92 [THT]"]
  Q5 = NPN-Transistor [package="TO92 [THT]"]
  Q6 = NPN-Transistor [package="TO92 [THT]"]
  Q7 = NPN-Transistor [package="TO92 [THT]"]
  LED1 = LED - 5mm [color="Red (633nm)" package="5 mm [THT]"]
  R1 = Resistor [tolerance=±5% resistance=220 package=THT]
  LED2 = LED - 5mm [color="Red (633nm)" package="5 mm [THT]"]
  LED3 = LED - 5mm [color="Red (633nm)" package="5 mm [THT]"]
  LED1_2 = LED - 5mm [color="Red (633nm)" package="5 mm [THT]"]
  LED6 = LED - 5mm [color="Red (633nm)" package="5 mm [THT]"]
  COLB_1 = RGB LED (com. cathode, rgb) [package="5 mm [THT]"]  # not connected
  L1 = Solenoid [part_number="Door lock"]
  Door_relay = OMRON PCB Power Relay – G5LE [part_number="G5LE-1\n" package=THT]
  +7V = Power plug
  +12V = Power plug
  S1 = Round Pushbutton
  S3 = Round Pushbutton
  S2 = Round Pushbutton
  S4 = Round Pushbutton
  COLB_2 = RGB LED (com. cathode, rgb) [package="5 mm [THT]"]  # not connected
  COLB_3 = RGB LED (com. cathode, rgb) [package="5 mm [THT]"]  # not connected
  COLB_4 = RGB LED (com. cathode, rgb) [package="5 mm [THT]"]  # not connected
  START = Round Pushbutton
  LED5 = LED - 5mm [color="Red (633nm)" package="5 mm [THT]"]
  LED4 = LED - 5mm [color="Red (633nm)" package="5 mm [THT]"]
  RFM12b1 = RFM12b HopeRF Transceiver
  RFM12b2 = RFM12b HopeRF Transceiver
  RFM12b3 = RFM12b HopeRF Transceiver
  RFM12b4 = RFM12b HopeRF Transceiver
  Q8 = NPN-Transistor [package="TO92 [THT]"]

nets:
  N1: Часть2.A0, S1.leg1
  N2: Часть2.A1, S3.leg1
  N3: Часть2.A2, S4.leg1
  N4: Часть2.A3, S2.leg1
  N5: Часть2.A4, START.leg1
  N6: Часть2.+5V, LED1.anode, LED3.anode, LED1_2.anode, Door_relay.COIL2, LED5.anode
  GND: Часть2.GND, Часть2.N$107, Часть2.N$261, Часть2.N$263, Часть2.N$272, Часть2.N$297, Часть2.N$319, Часть2.N$383, Q1.C, Q2.C, Q3.C, Q6.C, Q7.C, +7V.GND, START.leg0, Q8.C
  +9V: Часть2.+9V, +7V.VCC
  N7: Часть2.D8, Часть2.N$310
  N8: Часть2.D9, Часть2.N$240, Q5.B
  N9: Часть2.D10, Door_relay.COIL1
  N10: Часть2.D13, R1.Pin_1
  N11: Часть2.D2, RFM12b4.12_SDI
  N12: Часть2.D3, RFM12b4.13_SCK
  N13: Часть2.D4, Часть2.N$317, Q3.B
  N14: Часть2.D5, Часть2.N$281, Q2.B
  N15: Часть2.D6, Часть2.N$94, Q1.B
  N16: Часть2.D7, Часть2.N$153, Q7.B
  N17: Часть2.N$178, Часть2.N$190, LED1.cathode, R1.Pin_0
  N18: Часть2.N$231, Q8.E
  N19: Часть2.N$232, Q8.B
  N20: Часть2.N$237, Q5.E, LED4.cathode
  N21: Часть2.N$269, Q6.E
  N22: Часть2.N$273, Q1.E, LED3.cathode
  N23: Часть2.N$282, Q2.E, LED2.cathode
  N24: Часть2.N$298, Q5.C
  N25: Часть2.N$304, Q7.E, LED1_2.cathode
  N26: Часть2.N$305, Q6.B
  N27: Часть2.N$307, LED6.cathode
  N28: Часть2.N$318, Q3.E, LED5.cathode
  N29: L1.pin1, +12V.VCC, RFM12b1.10_GND, RFM12b2.10_GND, RFM12b3.10_GND, RFM12b4.10_GND
  N30: L1.pin2, Door_relay.C
  N31: Door_relay.B, +12V.GND
  N32: RFM12b3.9_VDD, RFM12b4.9_VDD

notes:
  MYSTERIA SMALL COLBS
